// Logisim project Register.circ as structural Verilog: 2 circuits, main circuit Register
module Register (
  input  [1:0] in_1,
  input  in_2,
  output [1:0] out_3
);

  FlipFlopDT flipflopdt_1 (.D(in_1[0]), .Clock(in_2), .Q(out_3[0]));  // open: nQ
  FlipFlopDT flipflopdt_2 (.D(in_1[1]), .Clock(in_2), .Q(out_3[1]));  // open: nQ
endmodule

module RegisterFile (
);

  wire undriven, undriven_2, undriven_3, undriven_4, undriven_5, undriven_6, undriven_7, undriven_8,
       undriven_9, undriven_10, undriven_11, undriven_12, undriven_13, undriven_14, undriven_15, undriven_16,
       undriven_17, undriven_18, undriven_19, undriven_20, undriven_21, undriven_22, undriven_23,
       undriven_24, undriven_25, undriven_26, undriven_27, undriven_28, undriven_29, undriven_30,
       undriven_31, undriven_32, undriven_33, undriven_34, undriven_35, undriven_36, undriven_37,
       undriven_38, undriven_39, undriven_40, undriven_41, undriven_42, undriven_43, undriven_44,
       undriven_45, undriven_46, undriven_47, undriven_48;
  wire [1:0] register_1_out_3;

  Register register_1 (.in_2(undriven_13), .out_3(register_1_out_3));  // open: in_1
  Register register_2 (.in_2(undriven_14));  // open: in_1, out_3
  Register register_3 (.in_2(undriven_15));  // open: in_1, out_3
  Register register_4 (.in_2(undriven));  // open: in_1, out_3
  Register register_5 (.in_2(undriven_16));  // open: in_1, out_3
  Register register_6 (.in_2(undriven_17));  // open: in_1, out_3
  Register register_7 (.in_2(undriven_18));  // open: in_1, out_3
  Register register_8 (.in_2(undriven_2));  // open: in_1, out_3
  Register register_9 (.in_2(undriven_19));  // open: in_1, out_3
  Register register_10 (.in_2(undriven_20));  // open: in_1, out_3
  Register register_11 (.in_2(undriven_21));  // open: in_1, out_3
  Register register_12 (.in_2(undriven_3));  // open: in_1, out_3
  Register register_13 (.in_2(undriven_22));  // open: in_1, out_3
  Register register_14 (.in_2(undriven_23));  // open: in_1, out_3
  Register register_15 (.in_2(undriven_24));  // open: in_1, out_3
  Register register_16 (.in_2(undriven_4));  // open: in_1, out_3
  Register register_17 (.in_2(undriven_25));  // open: in_1, out_3
  Register register_18 (.in_2(undriven_26));  // open: in_1, out_3
  Register register_19 (.in_2(undriven_27));  // open: in_1, out_3
  Register register_20 (.in_2(undriven_5));  // open: in_1, out_3
  Register register_21 (.in_2(undriven_28));  // open: in_1, out_3
  Register register_22 (.in_2(undriven_29));  // open: in_1, out_3
  Register register_23 (.in_2(undriven_30));  // open: in_1, out_3
  Register register_24 (.in_2(undriven_6));  // open: in_1, out_3
  Register register_25 (.in_2(undriven_31));  // open: in_1, out_3
  Register register_26 (.in_2(undriven_32));  // open: in_1, out_3
  Register register_27 (.in_2(undriven_33));  // open: in_1, out_3
  Register register_28 (.in_2(undriven_7));  // open: in_1, out_3
  Register register_29 (.in_2(undriven_34));  // open: in_1, out_3
  Register register_30 (.in_2(undriven_35));  // open: in_1, out_3
  Register register_31 (.in_2(undriven_36));  // open: in_1, out_3
  Register register_32 (.in_2(undriven_8));  // open: in_1, out_3
  Register register_33 (.in_2(undriven_37));  // open: in_1, out_3
  Register register_34 (.in_2(undriven_38));  // open: in_1, out_3
  Register register_35 (.in_2(undriven_39));  // open: in_1, out_3
  Register register_36 (.in_2(undriven_9));  // open: in_1, out_3
  Register register_37 (.in_2(undriven_40));  // open: in_1, out_3
  Register register_38 (.in_2(undriven_41));  // open: in_1, out_3
  Register register_39 (.in_2(undriven_42));  // open: in_1, out_3
  Register register_40 (.in_2(undriven_10));  // open: in_1, out_3
  Register register_41 (.in_2(undriven_43));  // open: in_1, out_3
  Register register_42 (.in_2(undriven_44));  // open: in_1, out_3
  Register register_43 (.in_2(undriven_45));  // open: in_1, out_3
  Register register_44 (.in_2(undriven_11));  // open: in_1, out_3
  Register register_45 (.in_2(undriven_46));  // open: in_1, out_3
  Register register_46 (.in_2(undriven_47));  // open: in_1, out_3
  Register register_47 (.in_2(undriven_48));  // open: in_1, out_3
  Register register_48 (.in_2(undriven_12));  // open: in_1, out_3
endmodule
